# Fritzing sketch soccer clear (saved by Fritzing 0.9.3b)

parts:
  PCB1 = Arduino Mega 2560 (Rev3) [part_number="Arduino MEGA 2560"]
  R1 = Resistor [tolerance=±5% resistance=220 package=THT]
  LED1 = LED - 5mm [color="Green (555nm)" package="5 mm [THT]"]
  LCD1 = LCD screen
  LED2 = LED - 5mm [color="Green (555nm)" package="5 mm [THT]"]
  LED3 = LED - 5mm [color="Green (555nm)" package="5 mm [THT]"]
  LED4 = LED - 5mm [color="Green (555nm)" package="5 mm [THT]"]
  LED5 = LED - 5mm [color="Red (635nm)" package="5 mm [THT]"]
  LED7 = LED - 5mm [color="Green (555nm)" package="5 mm [THT]"]
  LED8 = LED - 5mm [color="Green (555nm)" package="5 mm [THT]"]
  LED9 = LED - 5mm [color="Green (555nm)" package="5 mm [THT]"]
  LED10 = LED - 5mm [color="Green (555nm)" package="5 mm [THT]"]
  LED11 = LED - 5mm [color="Green (555nm)" package="5 mm [THT]"]
  LED12 = LED - 5mm [color="Red (635nm)" package="5 mm [THT]"]
  LED13 = LED - 5mm [color="Red (635nm)" package="5 mm [THT]"]
  LED22 = LED - 5mm [color="Red (635nm)" package="5 mm [THT]"]
  LED23 = LED - 5mm [color="Red (635nm)" package="5 mm [THT]"]
  LED24 = LED - 5mm [color="Red (635nm)" package="5 mm [THT]"]
  LED25 = LED - 5mm [color="Red (635nm)" package="5 mm [THT]"]
  LED26 = LED - 5mm [color="Red (635nm)" package="5 mm [THT]"]
  LED27 = LED - 5mm [color="Red (635nm)" package="5 mm [THT]"]
  LED28 = LED - 5mm [color="Red (635nm)" package="5 mm [THT]"]
  LED29 = LED - 5mm [color="Green (555nm)" package="5 mm [THT]"]
  LED30 = LED - 5mm [color="Red (635nm)" package="5 mm [THT]"]
  LED31 = LED - 5mm [color="Green (555nm)" package="5 mm [THT]"]
  LED32 = LED - 5mm [color="Green (555nm)" package="5 mm [THT]"]
  LED33 = LED - 5mm [color="Red (635nm)" package="5 mm [THT]"]
  R2 = Resistor [tolerance=±5% resistance=220 package=THT]
  R3 = Resistor [tolerance=±5% resistance=220 package=THT]
  R4 = Resistor [tolerance=±5% resistance=220 package=THT]
  R5 = Resistor [tolerance=±5% resistance=220 package=THT]
  R6 = Resistor [tolerance=±5% resistance=220 package=THT]
  R7 = Resistor [tolerance=±5% resistance=220 package=THT]
  R8 = Resistor [tolerance=±5% resistance=220 package=THT]
  R9 = Resistor [tolerance=±5% resistance=220 package=THT]
  R10 = Resistor [tolerance=±5% resistance=220 package=THT]
  R11 = Resistor [tolerance=±5% resistance=220 package=THT]
  R12 = Resistor [tolerance=±5% resistance=220 package=THT]
  R13 = Resistor [tolerance=±5% resistance=220 package=THT]
  R14 = Resistor [tolerance=±5% resistance=220 package=THT]
  R15 = Resistor [tolerance=±5% resistance=220 package=THT]
  R16 = Resistor [tolerance=±5% resistance=220 package=THT]
  R17 = Resistor [tolerance=±5% resistance=220 package=THT]
  R19 = Resistor [tolerance=±5% resistance=220 package=THT]
  R20 = Resistor [tolerance=±5% resistance=220 package=THT]
  R21 = Resistor [tolerance=±5% resistance=220 package=THT]
  R22 = Resistor [tolerance=±5% resistance=220 package=THT]
  R23 = Resistor [tolerance=±5% resistance=220 package=THT]
  R24 = Resistor [tolerance=±5% resistance=220 package=THT]
  R25 = Resistor [tolerance=±5% resistance=220 package=THT]
  R26 = Resistor [tolerance=±5% resistance=220 package=THT]
  R27 = Resistor [tolerance=±5% resistance=220 package=THT]
  R28 = Resistor [tolerance=±5% resistance=220 package=THT]
  R29 = Resistor [tolerance=±5% resistance=220 package=THT]
  R30 = Resistor [tolerance=±5% resistance=220 package=THT]
  R31 = Resistor [tolerance=±5% resistance=220 package=THT]
  R32 = Resistor [tolerance=±5% resistance=220 package=THT]
  R33 = Resistor [tolerance=±5% resistance=220 package=THT]
  LED34 = RGB LED (com. cathode, rgb) [package="5 mm [THT]"]
  LED35 = RGB LED (com. cathode, rgb) [package="5 mm [THT]"]
  LED36 = RGB LED (com. cathode, rgb) [package="5 mm [THT]"]
  R34 = Resistor [tolerance=±5% resistance=220 package=THT]
  R35 = Resistor [tolerance=±5% resistance=220 package=THT]
  R36 = Resistor [tolerance=±5% resistance=220 package=THT]
  R37 = Rotary Potentiometer (Small) [maximum_resistance=10kΩ package=THT]
  J1 = Piezo Speaker
  S2 = Toggle Switch [package=THT]
  S3 = Pushbutton [package="[THT]"]
  S4 = Pushbutton [package="[THT]"]
  S5 = Pushbutton [package="[THT]"]
  S8 = Pushbutton [package="[THT]"]
  S9 = Pushbutton [package="[THT]"]
  S10 = Pushbutton [package="[THT]"]
  S11 = Pushbutton [package="[THT]"]
  S12 = Pushbutton [package="[THT]"]
  S13 = Pushbutton [package="[THT]"]
  S14 = Pushbutton [package="[THT]"]
  PCB2 = MicroSD Card Module [part_number="MicroSD shield"]
  V3 = DC Power [voltage=6]  # not connected
  S15 = Toggle Switch [package=THT]
  R18 = Resistor [tolerance=±5% resistance=220 package=THT]
  LED37 = RGB LED (com. cathode, rgb) [package="5 mm [THT]"]
  LCM1602_IIC1 = LCM1602 IIC [part_number="LCM1602 IIC" chip_label="LCM1602 IIC" package="DIP (Dual Inline) [THT]"]

nets (from the breadboard view):
  N1: PCB1.A8, S9.Pin_3, S9.Pin_4
  N2: PCB1.A9, S3.Pin_3, S3.Pin_4
  N3: PCB1.A15, R37.wiper
  N4: PCB1.A0, S13.Pin_1
  N5: PCB1.A1, S14.Pin_1, S14.Pin_2
  N6: PCB1.A2, S12.Pin_1, S12.Pin_2
  N7: PCB1.A3, S10.Pin_1, S10.Pin_2
  N8: PCB1.A4, S11.Pin_1, S11.Pin_2
  N9: PCB1.A5, S8.Pin_3
  N10: PCB1.A6, S5.Pin_3, S5.Pin_4
  N11: PCB1.A7, S4.Pin_3, S4.Pin_4
  N12: PCB1.D21/SCL, LCM1602_IIC1.SCL
  N13: PCB1.D20/SDA, LCM1602_IIC1.SDA
  GND: PCB1.GND, R1.Pin_1, R2.Pin_1, R3.Pin_1, R4.Pin_1, R5.Pin_1, R6.Pin_1, R7.Pin_1, R8.Pin_1, R9.Pin_0, R10.Pin_1, R11.Pin_0, R12.Pin_0, R13.Pin_0, R14.Pin_1, R15.Pin_1, R16.Pin_0, R17.Pin_0, R22.Pin_1, R24.Pin_1, R26.Pin_1, R29.Pin_1, R30.Pin_1, R33.Pin_1, LED34.common_cathode, LED35.common_cathode, LED36.common_cathode, R37.leg1, J1.pin1, S2.L2, S3.Pin_1, S3.Pin_2, S4.Pin_1, S4.Pin_2, S5.Pin_1, S5.Pin_2, S8.Pin_1, S8.Pin_2, S9.Pin_1, S9.Pin_2, S10.Pin_3, S10.Pin_4, S11.Pin_3, S11.Pin_4, S12.Pin_3, S12.Pin_4, S13.Pin_3, S14.Pin_3, S14.Pin_4, PCB2.GND, R18.Pin_1, LED37.common_cathode, LCM1602_IIC1.GND
  N14: PCB1.D13_PWM, R27.Pin_0
  N15: PCB1.D12_PWM, R19.Pin_0
  N16: PCB1.D11_PWM, R31.Pin_0
  N17: PCB1.D10_PWM, R20.Pin_0
  N18: PCB1.D9_PWM, R21.Pin_0
  N19: PCB1.D8_PWM, R23.Pin_0
  VCC: PCB1.5V, R37.leg2, PCB2.VCC, LCM1602_IIC1.VCC
  N20: PCB1.VIN, S15.COM
  N21: PCB1.D2_PWM, R36.Pin_1
  N22: PCB1.D3_PWM, R34.Pin_1
  N23: PCB1.D4_PWM, R35.Pin_1
  N24: PCB1.D5_PWM, R28.Pin_1
  N25: PCB1.D6_PWM, R32.Pin_1
  N26: PCB1.D7_PWM, R25.Pin_1
  N27: PCB1.D22, LED28.anode
  N28: PCB1.D23, LED9.anode
  N29: PCB1.D24, LED11.anode
  N30: PCB1.D25, LED33.anode
  N31: PCB1.D26, LED10.anode
  N32: PCB1.D27, LED24.anode
  N33: PCB1.D28, LED31.anode
  N34: PCB1.D29, LED13.anode
  N35: PCB1.D30, LED12.anode
  N36: PCB1.D31, LED29.anode
  N37: PCB1.D32, LED32.anode
  N38: PCB1.D33, LED5.anode
  N39: PCB1.D34, LED27.anode
  N40: PCB1.D35, LED2.anode
  N41: PCB1.D36, LED7.anode
  N42: PCB1.D37, LED25.anode
  N43: PCB1.D38, LED26.anode
  N44: PCB1.D39, LED1.anode
  N45: PCB1.D40, LED23.anode
  N46: PCB1.D41, LED22.anode
  N47: PCB1.D42, LED8.anode
  N48: PCB1.D43, LED3.anode
  N49: PCB1.D44, LED30.anode
  N50: PCB1.D45, LED4.anode
  N51: PCB1.D46, J1.pin2
  N52: PCB1.D49, S2.COM
  N53: PCB1.D50, PCB2.MISO
  N54: PCB1.D51, PCB2.MOSI
  N55: PCB1.D52, PCB2.SCK
  N56: PCB1.D53, PCB2.CS
  N57: R1.Pin_0, LED1.cathode
  N58: LCD1.VSS, LCM1602_IIC1.K
  N59: LCD1.VDD, LCM1602_IIC1.A
  N60: LCD1.V0, LCM1602_IIC1.D7
  N61: LCD1.RS, LCM1602_IIC1.D6
  N62: LCD1.R/W, LCM1602_IIC1.D5
  N63: LCD1.E, LCM1602_IIC1.D4
  N64: LCD1.DB0, LCM1602_IIC1.D3
  N65: LCD1.DB1, LCM1602_IIC1.D2
  N66: LCD1.DB2, LCM1602_IIC1.D1
  N67: LCD1.DB3, LCM1602_IIC1.D0
  N68: LCD1.DB4, LCM1602_IIC1.E
  N69: LCD1.DB5, LCM1602_IIC1.RW
  N70: LCD1.DB6, LCM1602_IIC1.RS
  N71: LCD1.DB7, LCM1602_IIC1.V0
  N72: LCD1.LED+, LCM1602_IIC1.VDD
  N73: LCD1.LED-, LCM1602_IIC1.VSS
  N74: LED2.cathode, R15.Pin_0
  N75: LED3.cathode, R5.Pin_0
  N76: LED4.cathode, R10.Pin_0
  N77: LED5.cathode, R13.Pin_1
  N78: LED7.cathode, R2.Pin_0
  N79: LED8.cathode, R3.Pin_0
  N80: LED9.cathode, R24.Pin_0
  N81: LED10.cathode, R29.Pin_0
  N82: LED11.cathode, R33.Pin_0
  N83: LED12.cathode, R17.Pin_1
  N84: LED13.cathode, R9.Pin_1
  N85: LED22.cathode, R14.Pin_0
  N86: LED23.cathode, R26.Pin_0
  N87: LED24.cathode, R30.Pin_0
  N88: LED25.cathode, R8.Pin_0
  N89: LED26.cathode, R4.Pin_0
  N90: LED27.cathode, R6.Pin_0
  N91: LED28.cathode, R18.Pin_0
  N92: LED29.cathode, R16.Pin_1
  N93: LED30.cathode, R7.Pin_0
  N94: LED31.cathode, R12.Pin_1
  N95: LED32.cathode, R11.Pin_1
  N96: LED33.cathode, R22.Pin_0
  N97: R19.Pin_1, LED36.green_anode
  N98: R20.Pin_1, LED37.blue_anode
  N99: R21.Pin_1, LED37.green_anode
  N100: R23.Pin_1, LED37.red_anode
  N101: R25.Pin_0, LED35.blue_anode
  N102: R27.Pin_1, LED36.blue_anode
  N103: R28.Pin_0, LED35.red_anode
  N104: R31.Pin_1, LED36.red_anode
  N105: R32.Pin_0, LED35.green_anode
  N106: LED34.red_anode, R36.Pin_0
  N107: LED34.green_anode, R34.Pin_0
  N108: LED34.blue_anode, R35.Pin_0

notes:
  l3
  p8-10
  l201
  p29
  l4
  p11-13
  l112
  p28
  l202
  p30
  l111
  p31
  l203
  p33
  l110
  p32
  l1
  p2-4
  l211
  p27
  l212
  p22
  l101
  p24
  l2
  p5-7
  l210
  p25
  l102
  p23
  l103
  p26
  l106
  p42
  l206
  p44
  l204
  p37
  l107
  p36
  l105
  p43
  l108
  p35
  l208
  p41
  l209
  p40
  l104
  p45
  l205
  p34
  l207
  p38
  l109
  p39
  b11
  pa0
  b12
  pa1
  b13
  pa2
  b15
  pa4
  b14
  pa3
  b23
  pa7
  b24
  pa8
  b22
  pa6
  b21
  pa5
  b25
  pa9
  1
  0
  2
  10
  9
  11
  7
  8
  4
  3
  6
  5

custom parts:
  LCM1602 IIC: I2C-Module to use a 1602 or 2004 LCD on with the wire.h libory Serial LCD Modul
